// Logisim project Project1.circ as structural Verilog: 3 circuits, main circuit main
module main (
);

  wire Execute_we, Memory_we_2, registerfile_1_p2, WE_q;
  wire [1:0] SLT_q;
  wire [3:0] Op_2_q;
  wire [4:0] Execute_rd, Memory_rd_2, rd_q, registerfile_1_p3, Sa_q;
  wire [31:0] A_q, B_q, C_q, Execute_c, Execute_pc, Memory_c_2, Memory_pc_2, mipsprogramrom_1_p1,
       mipsprogramrom_1_p2, PC_2_q, registerfile_1_p1;

  // MIPSProgramROM mipsprogramrom_1: pin names not known; wires that end beside it: mipsprogramrom_1_p1, mipsprogramrom_1_p2
  Register #(.width(32)) Op (.D(mipsprogramrom_1_p2));  // open: en, Q, clk, clr
  Register #(.width(32)) PC (.D(mipsprogramrom_1_p1));  // open: en, Q, clk, clr
  // RegisterFile registerfile_1: pin names not known; wires that end beside it: registerfile_1_p1, registerfile_1_p2, registerfile_1_p3
  Register #(.width(32)) A (.Q(A_q));  // open: D, en, clk, clr
  Register #(.width(32)) B (.Q(B_q));  // open: D, en, clk, clr
  Register #(.width(5)) Sa (.Q(Sa_q));  // open: D, en, clk, clr
  Register #(.width(4)) Op_2 (.Q(Op_2_q));  // open: D, en, clk, clr
  Register #(.width(2)) SLT (.Q(SLT_q));  // open: D, en, clk, clr
  Execute Execute (
    .A(A_q), .B(B_q), .Sa(Sa_q), .Op(Op_2_q), .SLT(SLT_q), .C(Execute_c), .rd(Execute_rd), .PC(Execute_pc),
    .WE(Execute_we));
  Register #(.width(32)) C (.D(Execute_c), .Q(C_q));  // open: en, clk, clr
  Register #(.width(5)) rd (.D(Execute_rd), .Q(rd_q));  // open: en, clk, clr
  Register #(.width(32)) PC_2 (.D(Execute_pc), .Q(PC_2_q));  // open: en, clk, clr
  Register #(.width(1)) WE (.D(Execute_we), .Q(WE_q));  // open: en, clk, clr
  Memory Memory (
    .C(C_q), .rd(rd_q), .PC(PC_2_q), .WE(WE_q), .C_2(Memory_c_2), .rd_2(Memory_rd_2), .PC_2(Memory_pc_2),
    .WE_2(Memory_we_2));
  Register #(.width(32)) C_2 (.D(Memory_c_2), .Q(registerfile_1_p1));  // open: en, clk, clr
  Register #(.width(5)) rd_2 (.D(Memory_rd_2), .Q(registerfile_1_p3));  // open: en, clk, clr
  Register #(.width(32)) PC_3 (.D(Memory_pc_2), .Q(mipsprogramrom_1_p1));  // open: en, clk, clr
  Register #(.width(1)) WE_2 (.D(Memory_we_2), .Q(registerfile_1_p2));  // open: en, clk, clr

  // Notes on the sheet:
  //   Stage: Fetch
  //   Stage: Decode
  //   Stage: Writeback
  //   Stage: Execute
  //   Stage: Memory
  //   Stage: Writeback
endmodule

module Memory (
  input  [31:0] C,
  input  [4:0] rd,
  input  [31:0] PC,
  input  WE,
  output [31:0] C_2,
  output [4:0] rd_2,
  output [31:0] PC_2,
  output WE_2
);


  assign C_2 = C;
  assign PC_2 = PC;
  assign rd_2 = rd;
  assign WE_2 = WE;
endmodule

module Execute (
  input  [31:0] A,
  input  [31:0] B,
  input  [4:0] Sa,
  input  [3:0] Op,
  input  [1:0] SLT,
  output [31:0] C,
  output [4:0] rd,
  output [31:0] PC,
  output WE
);
endmodule
